// Logisim project MK-3.circ as structural Verilog: 10 circuits, main circuit FLIX16_CPU
module FULLADDER (
  input  Ci,
  input  A,
  input  B,
  output S,
  output Co
);

  wire and_1_out, and_2_out, xor_1_out;

  xor xor_1 (xor_1_out, A, B);
  and and_1 (and_1_out, A, B);
  xor xor_2 (S, xor_1_out, Ci);
  and and_2 (and_2_out, xor_1_out, Ci);
  or or_1 (Co, and_2_out, and_1_out);
endmodule

module ALU1 (
  input  A,
  input  B,
  input  AINV,
  input  BINV,
  input  Ci,
  input  OP_XOR,
  input  OP_SUM,
  input  OP_OR,
  input  OP_AND,
  output Co,
  output R
);

  wire and_1_out, fulladder_1_s, or_1_out, xor_1_out, xor_2_out, xor_3_out;

  xor xor_1 (xor_1_out, A, AINV);
  FULLADDER fulladder_1 (.S(fulladder_1_s), .Co(Co), .Ci(Ci), .A(xor_1_out), .B(xor_2_out));
  assign R = OP_SUM ? fulladder_1_s : 1'bz;  // Controlled_Buffer controlled_buffer_1
  or or_1 (or_1_out, xor_1_out, xor_2_out);
  assign R = OP_OR ? or_1_out : 1'bz;  // Controlled_Buffer controlled_buffer_2
  and and_1 (and_1_out, xor_1_out, xor_2_out);
  assign R = OP_AND ? and_1_out : 1'bz;  // Controlled_Buffer controlled_buffer_3
  xor xor_2 (xor_2_out, B, BINV);
  assign R = OP_XOR ? xor_3_out : 1'bz;  // Controlled_Buffer controlled_buffer_4
  xor xor_3 (xor_3_out, xor_2_out, xor_1_out);
endmodule

module ALU16 (
  input  OP_AINV,
  input  OP_BINV,
  input  OP_SUM,
  input  OP_OR,
  input  OP_AND,
  input  Ci,
  input  OP_XOR,
  input  LSL,
  input  LSR,
  input  [15:0] A,
  input  [15:0] B,
  output [15:0] R,
  output [3:0] F
);

  wire alu1_1_co, alu1_2_co, alu1_3_co, alu1_4_co, alu1_5_co, alu1_6_co, alu1_7_co, alu1_8_co, alu1_9_co,
       alu1_10_co, alu1_11_co, alu1_12_co, alu1_13_co, alu1_14_co, alu1_15_co, alu1_16_co, del_not16_1_q,
       del_not16_2_q, del_not16_3_q, del_not16_4_q, nor_1_out, nor_2_out, or_1_out, xor_1_out;
  wire [3:0] pull_resistor_1_node;
  wire [15:0] AT, BT, controlled_buffer_10_out, controlled_buffer_11_out, pull_resistor_5_node,
       shifter_1_out, shifter_2_out;

  Pull_Resistor pull_resistor_1 (.node(pull_resistor_1_node[0]));
  Pull_Resistor pull_resistor_2 (.node(pull_resistor_1_node[1]));
  Pull_Resistor pull_resistor_3 (.node(pull_resistor_1_node[2]));
  Pull_Resistor pull_resistor_4 (.node(pull_resistor_1_node[3]));
  assign pull_resistor_1_node[0] = OP_SUM ? alu1_1_co : 1'bz;  // Controlled_Buffer controlled_buffer_1
  assign pull_resistor_1_node[1] = OP_SUM ? xor_1_out : 1'bz;  // Controlled_Buffer controlled_buffer_2
  assign pull_resistor_1_node[2] = OP_SUM ? pull_resistor_5_node[15] : 1'bz;  // Controlled_Buffer controlled_buffer_3
  assign pull_resistor_1_node[3] = OP_SUM ? nor_1_out : 1'bz;  // Controlled_Buffer controlled_buffer_4
  DEL_NOT16 del_not16_1 (.Q(del_not16_1_q), .D(del_not16_2_q));
  DEL_NOT16 del_not16_2 (.Q(del_not16_2_q), .D(del_not16_3_q));
  DEL_NOT16 del_not16_3 (.Q(del_not16_3_q), .D(del_not16_4_q));
  DEL_NOT16 del_not16_4 (.Q(del_not16_4_q), .D(OP_SUM));
  xor xor_1 (xor_1_out, alu1_1_co, alu1_2_co);
  nor nor_1 (nor_1_out, pull_resistor_5_node[0], pull_resistor_5_node[1], pull_resistor_5_node[2], pull_resistor_5_node[3], pull_resistor_5_node[4], pull_resistor_5_node[5], pull_resistor_5_node[6], pull_resistor_5_node[7], pull_resistor_5_node[8], pull_resistor_5_node[9], pull_resistor_5_node[10], pull_resistor_5_node[11], pull_resistor_5_node[12], pull_resistor_5_node[13], pull_resistor_5_node[14], pull_resistor_5_node[15]);
  assign AT = or_1_out ? A : 16'bz;  // Controlled_Buffer controlled_buffer_5
  assign BT = or_1_out ? B : 16'bz;  // Controlled_Buffer controlled_buffer_6
  Register #(.width(4)) register_1 (.D(pull_resistor_1_node), .en(OP_SUM), .clk(del_not16_1_q), .Q(F));  // open: clr
  or or_1 (or_1_out, OP_BINV, OP_AINV, OP_OR, OP_AND, OP_SUM);
  ALU1 alu1_1 (
    .Co(alu1_1_co), .R(pull_resistor_5_node[15]), .A(AT[15]), .B(BT[15]), .AINV(OP_AINV), .BINV(OP_BINV),
    .Ci(alu1_2_co), .OP_XOR(OP_XOR), .OP_SUM(OP_SUM), .OP_OR(OP_OR), .OP_AND(OP_AND));
  ALU1 alu1_2 (
    .Co(alu1_2_co), .R(pull_resistor_5_node[14]), .A(AT[14]), .B(BT[14]), .AINV(OP_AINV), .BINV(OP_BINV),
    .Ci(alu1_3_co), .OP_XOR(OP_XOR), .OP_SUM(OP_SUM), .OP_OR(OP_OR), .OP_AND(OP_AND));
  ALU1 alu1_3 (
    .Co(alu1_3_co), .R(pull_resistor_5_node[13]), .A(AT[13]), .B(BT[13]), .AINV(OP_AINV), .BINV(OP_BINV),
    .Ci(alu1_4_co), .OP_XOR(OP_XOR), .OP_SUM(OP_SUM), .OP_OR(OP_OR), .OP_AND(OP_AND));
  ALU1 alu1_4 (
    .Co(alu1_4_co), .R(pull_resistor_5_node[12]), .A(AT[12]), .B(BT[12]), .AINV(OP_AINV), .BINV(OP_BINV),
    .Ci(alu1_5_co), .OP_XOR(OP_XOR), .OP_SUM(OP_SUM), .OP_OR(OP_OR), .OP_AND(OP_AND));
  ALU1 alu1_5 (
    .Co(alu1_5_co), .R(pull_resistor_5_node[11]), .A(AT[11]), .B(BT[11]), .AINV(OP_AINV), .BINV(OP_BINV),
    .Ci(alu1_6_co), .OP_XOR(OP_XOR), .OP_SUM(OP_SUM), .OP_OR(OP_OR), .OP_AND(OP_AND));
  ALU1 alu1_6 (
    .Co(alu1_6_co), .R(pull_resistor_5_node[10]), .A(AT[10]), .B(BT[10]), .AINV(OP_AINV), .BINV(OP_BINV),
    .Ci(alu1_7_co), .OP_XOR(OP_XOR), .OP_SUM(OP_SUM), .OP_OR(OP_OR), .OP_AND(OP_AND));
  ALU1 alu1_7 (
    .Co(alu1_7_co), .R(pull_resistor_5_node[9]), .A(AT[9]), .B(BT[9]), .AINV(OP_AINV), .BINV(OP_BINV),
    .Ci(alu1_8_co), .OP_XOR(OP_XOR), .OP_SUM(OP_SUM), .OP_OR(OP_OR), .OP_AND(OP_AND));
  assign R = LSL ? shifter_1_out : 16'bz;  // Controlled_Buffer controlled_buffer_7
  assign R = LSR ? shifter_2_out : 16'bz;  // Controlled_Buffer controlled_buffer_8
  assign R = nor_2_out ? pull_resistor_5_node : 16'bz;  // Controlled_Buffer controlled_buffer_9
  ALU1 alu1_8 (
    .Co(alu1_8_co), .R(pull_resistor_5_node[8]), .A(AT[8]), .B(BT[8]), .AINV(OP_AINV), .BINV(OP_BINV),
    .Ci(alu1_9_co), .OP_XOR(OP_XOR), .OP_SUM(OP_SUM), .OP_OR(OP_OR), .OP_AND(OP_AND));
  assign controlled_buffer_10_out = LSL ? pull_resistor_5_node : 16'bz;  // Controlled_Buffer controlled_buffer_10
  assign controlled_buffer_11_out = LSR ? pull_resistor_5_node : 16'bz;  // Controlled_Buffer controlled_buffer_11
  nor nor_2 (nor_2_out, LSR, LSL);
  Shifter #(.width(16)) shifter_1 (.in(controlled_buffer_10_out), .\dist (4'b0001), .out(shifter_1_out));
  Pull_Resistor pull_resistor_5 (.node(pull_resistor_5_node));
  Shifter #(.shift("lr"), .width(16)) shifter_2 (.in(controlled_buffer_11_out), .\dist (4'b0001), .out(shifter_2_out));
  ALU1 alu1_9 (
    .Co(alu1_9_co), .R(pull_resistor_5_node[7]), .A(AT[7]), .B(BT[7]), .AINV(OP_AINV), .BINV(OP_BINV),
    .Ci(alu1_10_co), .OP_XOR(OP_XOR), .OP_SUM(OP_SUM), .OP_OR(OP_OR), .OP_AND(OP_AND));
  ALU1 alu1_10 (
    .Co(alu1_10_co), .R(pull_resistor_5_node[6]), .A(AT[6]), .B(BT[6]), .AINV(OP_AINV), .BINV(OP_BINV),
    .Ci(alu1_11_co), .OP_XOR(OP_XOR), .OP_SUM(OP_SUM), .OP_OR(OP_OR), .OP_AND(OP_AND));
  ALU1 alu1_11 (
    .Co(alu1_11_co), .R(pull_resistor_5_node[5]), .A(AT[5]), .B(BT[5]), .AINV(OP_AINV), .BINV(OP_BINV),
    .Ci(alu1_12_co), .OP_XOR(OP_XOR), .OP_SUM(OP_SUM), .OP_OR(OP_OR), .OP_AND(OP_AND));
  ALU1 alu1_12 (
    .Co(alu1_12_co), .R(pull_resistor_5_node[4]), .A(AT[4]), .B(BT[4]), .AINV(OP_AINV), .BINV(OP_BINV),
    .Ci(alu1_13_co), .OP_XOR(OP_XOR), .OP_SUM(OP_SUM), .OP_OR(OP_OR), .OP_AND(OP_AND));
  ALU1 alu1_13 (
    .Co(alu1_13_co), .R(pull_resistor_5_node[3]), .A(AT[3]), .B(BT[3]), .AINV(OP_AINV), .BINV(OP_BINV),
    .Ci(alu1_14_co), .OP_XOR(OP_XOR), .OP_SUM(OP_SUM), .OP_OR(OP_OR), .OP_AND(OP_AND));
  ALU1 alu1_14 (
    .Co(alu1_14_co), .R(pull_resistor_5_node[2]), .A(AT[2]), .B(BT[2]), .AINV(OP_AINV), .BINV(OP_BINV),
    .Ci(alu1_15_co), .OP_XOR(OP_XOR), .OP_SUM(OP_SUM), .OP_OR(OP_OR), .OP_AND(OP_AND));
  ALU1 alu1_15 (
    .Co(alu1_15_co), .R(pull_resistor_5_node[1]), .A(AT[1]), .B(BT[1]), .AINV(OP_AINV), .BINV(OP_BINV),
    .Ci(alu1_16_co), .OP_XOR(OP_XOR), .OP_SUM(OP_SUM), .OP_OR(OP_OR), .OP_AND(OP_AND));
  ALU1 alu1_16 (
    .Co(alu1_16_co), .R(pull_resistor_5_node[0]), .A(AT[0]), .B(BT[0]), .AINV(OP_AINV), .BINV(OP_BINV),
    .Ci(Ci), .OP_XOR(OP_XOR), .OP_SUM(OP_SUM), .OP_OR(OP_OR), .OP_AND(OP_AND));

  // Other names for the same wires on the sheet: AIT = OP_AINV; ANT = OP_AND; BIT = OP_BINV; CiT = Ci; LST = LSL;
  //   ORT = OP_OR; RST = LSR; RT[15:0] = R; SUT = OP_SUM; XOT = OP_XOR
endmodule

module ODL (
  input  [7:0] OPCODE,
  output NOP,
  output LDAI,
  output LDBI,
  output LDCI,
  output LDAR,
  output LDBR,
  output LDCR,
  output STA,
  output STB,
  output STC,
  output ALU_ADD,
  output ALU_SUB,
  output ALU_AND,
  output ALU_OR,
  output ALU_NOT,
  output ALU_NOR,
  output ALU_NAND,
  output JMP,
  output JZ,
  output JN,
  output ALU_XOR,
  output HLT,
  output IN_C,
  output OUT_C,
  output JNZ,
  output LSL,
  output LSR,
  output PUSHREG,
  output POPREG,
  output PUSHI,
  output POPI
);

  Decoder #(.enable("false"), .select(5)) decoder_1 (
    .out0(NOP), .out1(LDAI), .out2(LDBI), .out3(LDCI), .out4(LDAR), .out5(LDBR), .out6(LDCR), .out7(STA),
    .out8(STB), .out9(STC), .out10(ALU_ADD), .out11(ALU_SUB), .out12(ALU_AND), .out13(ALU_OR),
    .out14(ALU_NOT), .out15(ALU_NOR), .out16(ALU_NAND), .out17(JMP), .out18(JZ), .out19(JN), .out20(ALU_XOR),
    .out21(HLT), .out22(IN_C), .out23(OUT_C), .out24(JNZ), .out25(LSL), .out26(LSR), .out27(PUSHREG),
    .out28(POPREG), .out29(PUSHI), .out30(POPI), .sel(OPCODE[4:0]));  // open: out31
endmodule

module FLIX16_CPU (
  input  [15:0] EXTIN,
  input  CLK,
  input  [15:0] RAM_OUT,
  input  CTR_RST,
  input  E,
  input  INT1,
  input  [23:0] INSTR,
  output [15:0] RAM_ADDR,
  output RAM_WE,
  output [15:0] INTO,
  output RAM_CLK,
  output WO,
  output [15:0] RAM_IN,
  output [15:0] IPOUT
);

  wire A_AND_out, A_OR_out, A_SUM_out, Ai_out, and_1_out, Bi_out, Ci_out, controlled_buffer_6_out,
       controlled_buffer_14_out, controlled_buffer_26_out, decoder_1_out1, decoder_1_out2, decoder_1_out3,
       decoder_2_out1, decoder_2_out2, decoder_2_out3, del_not16_2_q, del_not16_3_q, del_not16_4_q,
       del_not16_5_q, del_not16_6_q, del_not16_7_q, del_not16_8_q, del_not16_9_q, del_not16_10_q,
       del_not16_11_q, del_not16_12_q, del_not16_13_q, del_not16_14_q, del_not16_16_q, demultiplexer_1_out0,
       demultiplexer_1_out1, demultiplexer_1_out2, demultiplexer_2_out0, demultiplexer_2_out1,
       demultiplexer_2_out2, JN_out, JNZ_out, JZ_out, nor_1_out, not_1_out, not_2_out, not_3_out, not_4_out,
       odl_1_alu_add, odl_1_alu_and, odl_1_alu_nand, odl_1_alu_nor, odl_1_alu_not, odl_1_alu_or,
       odl_1_alu_sub, odl_1_alu_xor, odl_1_hlt, odl_1_in_c, odl_1_jmp, odl_1_jn, odl_1_jnz, odl_1_jz,
       odl_1_ldai, odl_1_ldar, odl_1_ldbi, odl_1_ldbr, odl_1_ldci, odl_1_ldcr, odl_1_lsl, odl_1_lsr,
       odl_1_out_c, odl_1_popi, odl_1_popreg, odl_1_pushi, odl_1_pushreg, odl_1_sta, odl_1_stb, odl_1_stc,
       or_1_out, or_2_out, or_3_out, or_4_out, or_5_out, or_6_out, or_7_out, or_8_out, or_9_out, or_10_out,
       or_11_out, or_13_out, or_14_out, or_16_out, PO_out, PU_out, xor_1_out;
  wire [1:0] pull_resistor_3_node, pull_resistor_3_node_2, pull_resistor_3_node_3, pull_resistor_3_node_4,
       pull_resistor_3_node_5, pull_resistor_3_node_6, pull_resistor_3_node_7, pull_resistor_3_node_8,
       pull_resistor_4_node, pull_resistor_5_node;
  wire [3:0] alu16_1_f;
  wire [15:0] A_q, alu16_1_r, B_q, C_q, controlled_buffer_1_out, controlled_buffer_2_out,
       controlled_buffer_7_out, controlled_buffer_8_out, controlled_buffer_9_out, controlled_buffer_10_out,
       controlled_buffer_17_out, controlled_buffer_18_out, controlled_buffer_19_out,
       controlled_buffer_35_out, controlled_buffer_36_out, controlled_buffer_38_out, counter_1_q,
       STACK_hwstk_o, STACK_ram_addr_i, STACK_ram_data_i;

  LED ZFL (.in(alu16_1_f[3]));
  LED VFL (.in(alu16_1_f[2]));
  LED NFL (.in(alu16_1_f[1]));
  LED CoL (.in(alu16_1_f[0]));
  DEL_NOT16 del_not16_1 (.Q(WO), .D(del_not16_2_q));
  DEL_NOT16 del_not16_2 (.Q(del_not16_2_q), .D(odl_1_out_c));
  // Probe on controlled_buffer_17_out
  ALU16 alu16_1 (
    .R(alu16_1_r), .F(alu16_1_f), .A(controlled_buffer_18_out), .B(controlled_buffer_17_out),
    .OP_AINV(Ai_out), .OP_BINV(Bi_out), .OP_SUM(A_SUM_out), .OP_OR(A_OR_out), .OP_AND(A_AND_out),
    .Ci(Ci_out), .OP_XOR(odl_1_alu_xor), .LSL(odl_1_lsl), .LSR(odl_1_lsr));
  // Probe on alu16_1_r
  Pull_Resistor pull_resistor_1 (.node(alu16_1_f[3]));
  // Probe on controlled_buffer_18_out
  assign controlled_buffer_1_out = demultiplexer_1_out0 ? controlled_buffer_2_out : 16'bz;  // Controlled_Buffer controlled_buffer_1
  Pull_Resistor pull_resistor_2 (.node(alu16_1_f[2]));
  nor nor_1 (nor_1_out, Ci_out, Ai_out, Bi_out, A_SUM_out, A_AND_out, A_OR_out, odl_1_alu_xor);
  not not_1 (not_1_out, nor_1_out);
  assign controlled_buffer_2_out = not_1_out ? alu16_1_r : 16'bz;  // Controlled_Buffer controlled_buffer_2
  assign controlled_buffer_1_out = decoder_2_out1 ? STACK_hwstk_o : 16'bz;  // Controlled_Buffer controlled_buffer_3
  Register #(.width(16)) A (
    .D(controlled_buffer_1_out), .en(or_1_out), .clk(controlled_buffer_6_out), .Q(A_q));  // open: clr
  assign controlled_buffer_1_out = odl_1_ldar ? controlled_buffer_36_out : 16'bz;  // Controlled_Buffer controlled_buffer_4
  assign controlled_buffer_1_out = odl_1_ldai ? INSTR[15:0] : 16'bz;  // Controlled_Buffer controlled_buffer_5
  assign controlled_buffer_6_out = or_1_out ? del_not16_3_q : 1'bz;  // Controlled_Buffer controlled_buffer_6
  DEL_NOT16 del_not16_3 (.Q(del_not16_3_q), .D(del_not16_4_q));
  DEL_NOT16 del_not16_4 (.Q(del_not16_4_q), .D(del_not16_5_q));
  DEL_NOT16 del_not16_5 (.Q(del_not16_5_q), .D(del_not16_6_q));
  DEL_NOT16 del_not16_6 (.Q(del_not16_6_q), .D(or_1_out));
  or or_1 (or_1_out, odl_1_ldar, demultiplexer_1_out0, odl_1_ldai, decoder_2_out1);
  not not_2 (not_2_out, xor_1_out);
  xor xor_1 (xor_1_out, INT1, odl_1_hlt);
  assign controlled_buffer_7_out = decoder_1_out1 ? A_q : 16'bz;  // Controlled_Buffer controlled_buffer_7
  and and_1 (and_1_out, CLK, not_2_out);
  and JNZ (JNZ_out, not_3_out, odl_1_jnz);
  and JZ (JZ_out, alu16_1_f[3], odl_1_jz);
  not not_3 (not_3_out, alu16_1_f[3]);
  assign controlled_buffer_8_out = or_2_out ? A_q : 16'bz;  // Controlled_Buffer controlled_buffer_8
  buf or_2 (or_2_out, odl_1_sta);  // OR_Gate
  Counter #(.max('hffff), .width(16)) counter_1 (
    .clr(CTR_RST), .load(or_3_out), .up(1'b1), .count(E), .clk(and_1_out), .D(controlled_buffer_9_out),
    .Q(counter_1_q));  // open: carry
  assign controlled_buffer_9_out = or_3_out ? INSTR[15:0] : 16'bz;  // Controlled_Buffer controlled_buffer_9
  or or_3 (or_3_out, JNZ_out, odl_1_jmp, JZ_out, JN_out);
  and JN (JN_out, alu16_1_f[2], odl_1_jn);
  assign controlled_buffer_10_out = demultiplexer_1_out1 ? controlled_buffer_2_out : 16'bz;  // Controlled_Buffer controlled_buffer_10
  assign controlled_buffer_10_out = odl_1_ldbr ? controlled_buffer_36_out : 16'bz;  // Controlled_Buffer controlled_buffer_11
  assign controlled_buffer_10_out = decoder_2_out2 ? STACK_hwstk_o : 16'bz;  // Controlled_Buffer controlled_buffer_12
  Register #(.width(16)) B (
    .D(controlled_buffer_10_out), .en(or_4_out), .clk(controlled_buffer_14_out), .Q(B_q));  // open: clr
  assign controlled_buffer_10_out = odl_1_ldbi ? INSTR[15:0] : 16'bz;  // Controlled_Buffer controlled_buffer_13
  assign controlled_buffer_14_out = or_4_out ? del_not16_7_q : 1'bz;  // Controlled_Buffer controlled_buffer_14
  DEL_NOT16 del_not16_7 (.Q(del_not16_7_q), .D(del_not16_8_q));
  DEL_NOT16 del_not16_8 (.Q(del_not16_8_q), .D(del_not16_9_q));
  DEL_NOT16 del_not16_9 (.Q(del_not16_9_q), .D(del_not16_10_q));
  DEL_NOT16 del_not16_10 (.Q(del_not16_10_q), .D(or_4_out));
  or or_4 (or_4_out, odl_1_ldbr, demultiplexer_1_out1, odl_1_ldbi, decoder_2_out2);
  assign controlled_buffer_8_out = or_5_out ? B_q : 16'bz;  // Controlled_Buffer controlled_buffer_15
  assign controlled_buffer_7_out = decoder_1_out2 ? B_q : 16'bz;  // Controlled_Buffer controlled_buffer_16
  Register #(.width(16)) IP (.D(counter_1_q), .en(and_1_out), .clk(and_1_out), .Q(IPOUT));  // open: clr
  Demultiplexer #(.select(2)) demultiplexer_1 (
    .out0(demultiplexer_1_out0), .out1(demultiplexer_1_out1), .out2(demultiplexer_1_out2), .in(or_8_out),
    .sel(pull_resistor_3_node));  // open: out3
  assign controlled_buffer_17_out = demultiplexer_1_out0 ? A_q : 16'bz;  // Controlled_Buffer controlled_buffer_17
  buf or_5 (or_5_out, odl_1_stb);  // OR_Gate
  Demultiplexer #(.select(2)) demultiplexer_2 (
    .out0(demultiplexer_2_out0), .out1(demultiplexer_2_out1), .out2(demultiplexer_2_out2), .in(or_8_out),
    .sel(pull_resistor_3_node_5));  // open: out3
  assign controlled_buffer_18_out = demultiplexer_2_out0 ? A_q : 16'bz;  // Controlled_Buffer controlled_buffer_18
  assign controlled_buffer_19_out = demultiplexer_1_out2 ? controlled_buffer_2_out : 16'bz;  // Controlled_Buffer controlled_buffer_19
  assign controlled_buffer_19_out = odl_1_ldcr ? controlled_buffer_36_out : 16'bz;  // Controlled_Buffer controlled_buffer_20
  assign controlled_buffer_19_out = odl_1_in_c ? EXTIN : 16'bz;  // Controlled_Buffer controlled_buffer_21
  assign controlled_buffer_17_out = demultiplexer_1_out1 ? B_q : 16'bz;  // Controlled_Buffer controlled_buffer_22
  assign controlled_buffer_18_out = demultiplexer_2_out1 ? B_q : 16'bz;  // Controlled_Buffer controlled_buffer_23
  assign controlled_buffer_19_out = decoder_2_out3 ? STACK_hwstk_o : 16'bz;  // Controlled_Buffer controlled_buffer_24
  Register #(.width(16)) C (
    .D(controlled_buffer_19_out), .en(or_6_out), .clk(controlled_buffer_26_out), .Q(C_q));  // open: clr
  assign controlled_buffer_19_out = odl_1_ldci ? INSTR[15:0] : 16'bz;  // Controlled_Buffer controlled_buffer_25
  assign controlled_buffer_26_out = or_6_out ? del_not16_11_q : 1'bz;  // Controlled_Buffer controlled_buffer_26
  DEL_NOT16 del_not16_11 (.Q(del_not16_11_q), .D(del_not16_12_q));
  DEL_NOT16 del_not16_12 (.Q(del_not16_12_q), .D(del_not16_13_q));
  DEL_NOT16 del_not16_13 (.Q(del_not16_13_q), .D(del_not16_14_q));
  DEL_NOT16 del_not16_14 (.Q(del_not16_14_q), .D(or_6_out));
  or or_6 (or_6_out, odl_1_ldcr, demultiplexer_1_out2, odl_1_ldci, decoder_2_out3);
  assign controlled_buffer_17_out = demultiplexer_1_out2 ? C_q : 16'bz;  // Controlled_Buffer controlled_buffer_27
  assign controlled_buffer_8_out = or_7_out ? C_q : 16'bz;  // Controlled_Buffer controlled_buffer_28
  assign INTO = odl_1_out_c ? C_q : 16'bz;  // Controlled_Buffer controlled_buffer_29
  assign controlled_buffer_7_out = decoder_1_out3 ? C_q : 16'bz;  // Controlled_Buffer controlled_buffer_30
  buf or_7 (or_7_out, odl_1_stc);  // OR_Gate
  assign controlled_buffer_18_out = demultiplexer_2_out2 ? C_q : 16'bz;  // Controlled_Buffer controlled_buffer_31
  Pull_Resistor pull_resistor_3 (.node({pull_resistor_3_node_8, pull_resistor_3_node_7, pull_resistor_3_node_6, pull_resistor_3_node_5, pull_resistor_3_node_4, pull_resistor_3_node_3, pull_resistor_3_node_2, pull_resistor_3_node}));
  assign {pull_resistor_3_node_8, pull_resistor_3_node_7, pull_resistor_3_node_6, pull_resistor_3_node_5, pull_resistor_3_node_4, pull_resistor_3_node_3, pull_resistor_3_node_2, pull_resistor_3_node} = or_8_out ? INSTR[15:0] : 16'bz;  // Controlled_Buffer controlled_buffer_32
  Pull_Resistor pull_resistor_4 (.node(pull_resistor_4_node));
  Decoder #(.enable("false"), .select(2)) decoder_1 (
    .out1(decoder_1_out1), .out2(decoder_1_out2), .out3(decoder_1_out3), .sel(pull_resistor_4_node));  // open: out0
  // Probe on INSTR[15:0]
  // Probe on INSTR[23:16]
  or or_8 (or_8_out, odl_1_alu_add, odl_1_alu_sub, odl_1_alu_and, odl_1_alu_or, odl_1_alu_not, or_9_out, odl_1_alu_nor, odl_1_alu_nand, odl_1_alu_xor);
  or or_9 (or_9_out, odl_1_lsr, odl_1_lsl);
  ODL odl_1 (
    .OPCODE(INSTR[23:16]), .LDAI(odl_1_ldai), .LDBI(odl_1_ldbi), .LDCI(odl_1_ldci), .LDAR(odl_1_ldar),
    .LDBR(odl_1_ldbr), .LDCR(odl_1_ldcr), .STA(odl_1_sta), .STB(odl_1_stb), .STC(odl_1_stc),
    .ALU_ADD(odl_1_alu_add), .ALU_SUB(odl_1_alu_sub), .ALU_AND(odl_1_alu_and), .ALU_OR(odl_1_alu_or),
    .ALU_NOT(odl_1_alu_not), .ALU_NOR(odl_1_alu_nor), .ALU_NAND(odl_1_alu_nand), .JMP(odl_1_jmp),
    .JZ(odl_1_jz), .JN(odl_1_jn), .ALU_XOR(odl_1_alu_xor), .HLT(odl_1_hlt), .IN_C(odl_1_in_c),
    .OUT_C(odl_1_out_c), .JNZ(odl_1_jnz), .LSL(odl_1_lsl), .LSR(odl_1_lsr), .PUSHREG(odl_1_pushreg),
    .POPREG(odl_1_popreg), .PUSHI(odl_1_pushi), .POPI(odl_1_popi));  // open: NOP
  or A_OR (A_OR_out, or_9_out, odl_1_alu_not, odl_1_alu_nand, odl_1_alu_or);
  or A_AND (A_AND_out, odl_1_alu_nor, odl_1_alu_and);
  or A_SUM (A_SUM_out, odl_1_alu_sub, odl_1_alu_add);
  assign pull_resistor_4_node = PU_out ? INSTR[9:8] : 2'bz;  // Controlled_Buffer controlled_buffer_33
  Pull_Resistor pull_resistor_5 (.node(pull_resistor_5_node));
  assign pull_resistor_5_node = PO_out ? INSTR[9:8] : 2'bz;  // Controlled_Buffer controlled_buffer_34
  Decoder #(.enable("false"), .select(2)) decoder_2 (
    .out1(decoder_2_out1), .out2(decoder_2_out2), .out3(decoder_2_out3), .sel(pull_resistor_5_node));  // open: out0
  LED led_1 (.in(odl_1_hlt));
  or Bi (Bi_out, odl_1_alu_nand, odl_1_alu_not, odl_1_alu_nor, odl_1_alu_sub);
  or or_10 (or_10_out, odl_1_ldar, odl_1_ldbr, odl_1_ldcr);
  or or_11 (or_11_out, odl_1_sta, odl_1_stb, odl_1_stc);
  or Ai (Ai_out, odl_1_alu_nor, odl_1_alu_nand, odl_1_alu_not);
  assign controlled_buffer_35_out = or_11_out ? controlled_buffer_8_out : 16'bz;  // Controlled_Buffer controlled_buffer_35
  buf Ci (Ci_out, odl_1_alu_sub);  // OR_Gate
  Pull_Resistor pull_resistor_6 (.node(INSTR[15:0]));
  Pull_Resistor pull_resistor_7 (.node(controlled_buffer_35_out));
  // OR_Gate or_12 has open pins: in0=PU_out, in1=PO_out, out=open
  or PU (PU_out, odl_1_pushreg, odl_1_pushi);
  or PO (PO_out, odl_1_popreg, odl_1_popi);
  assign controlled_buffer_36_out = or_10_out ? RAM_OUT : 16'bz;  // Controlled_Buffer controlled_buffer_36
  DEL_NOT16 del_not16_15 (.Q(RAM_CLK), .D(del_not16_16_q));
  DEL_NOT16 del_not16_16 (.Q(del_not16_16_q), .D(or_16_out));
  assign RAM_IN = or_11_out ? controlled_buffer_35_out : 16'bz;  // Controlled_Buffer controlled_buffer_37
  HWSTACK STACK (
    .HWSTK_O(STACK_hwstk_o), .RAM_ADDR_I(STACK_ram_addr_i), .RAM_DATA_I(STACK_ram_data_i),
    .RAM_O(controlled_buffer_38_out), .POP(PO_out), .PUSH(PU_out), .HWSTK_I(controlled_buffer_7_out));
  assign controlled_buffer_38_out = PO_out ? RAM_OUT : 16'bz;  // Controlled_Buffer controlled_buffer_38
  assign RAM_ADDR = not_4_out ? INSTR[15:0] : 16'bz;  // Controlled_Buffer controlled_buffer_39
  not not_4 (not_4_out, or_13_out);
  or or_13 (or_13_out, PU_out, PO_out);
  or or_14 (or_14_out, PU_out, PO_out);
  // Probe on STACK_hwstk_o
  assign RAM_ADDR = or_13_out ? STACK_ram_addr_i : 16'bz;  // Controlled_Buffer controlled_buffer_40
  or or_15 (RAM_WE, or_11_out, or_14_out);
  or or_16 (or_16_out, and_1_out, or_14_out);
  assign RAM_IN = PU_out ? STACK_ram_data_i : 16'bz;  // Controlled_Buffer controlled_buffer_41

  // Notes on the sheet:
  //   WO: pull=down
  //   EXTIN: pull=down
  //   INTO: pull=down
  //   0..3
  //   ZF, VF, NF, Co
  //   ASEL
  //   BSEL
  //   OP
  //   LDAR, LDBR, LDCR
  //   STA, STB, STC
  //   LDAI, LDBI, LDCI
  //   Stack data line of suffering
  //   ADD; SUB; AND; OR; NOT; NOR; NAND
endmodule

module DEL_NOT16 (
  input  D,
  output Q
);

  wire not_1_out, not_2_out, not_3_out, not_4_out, not_5_out, not_6_out, not_8_out, not_9_out, not_10_out,
       not_11_out, not_12_out, not_13_out, not_14_out, not_15_out, not_16_out, not_17_out, not_18_out,
       not_19_out, not_20_out, not_21_out, not_22_out, not_23_out, not_24_out;

  not not_1 (not_1_out, not_4_out);
  not not_2 (not_2_out, not_5_out);
  not not_3 (not_3_out, not_6_out);
  not not_4 (not_4_out, not_2_out);
  not not_5 (not_5_out, not_3_out);
  not not_6 (not_6_out, not_13_out);
  not not_7 (Q, not_10_out);
  not not_8 (not_8_out, not_11_out);
  not not_9 (not_9_out, not_12_out);
  not not_10 (not_10_out, not_8_out);
  not not_11 (not_11_out, not_9_out);
  not not_12 (not_12_out, not_19_out);
  not not_13 (not_13_out, not_16_out);
  not not_14 (not_14_out, not_17_out);
  not not_15 (not_15_out, not_18_out);
  not not_16 (not_16_out, not_14_out);
  not not_17 (not_17_out, not_15_out);
  not not_18 (not_18_out, D);
  not not_19 (not_19_out, not_22_out);
  not not_20 (not_20_out, not_23_out);
  not not_21 (not_21_out, not_24_out);
  not not_22 (not_22_out, not_20_out);
  not not_23 (not_23_out, not_21_out);
  not not_24 (not_24_out, not_1_out);
endmodule

module DISPCTR (
  input  [15:0] INSTR,
  output R,
  output E,
  output [6:0] X,
  output [6:0] Y,
  output [15:0] D
);

  wire decoder_1_out1, decoder_1_out2, decoder_1_out3, del_not16_2_q, del_not16_3_q, del_not16_4_q,
       del_not16_5_q, del_not16_6_q, del_not16_7_q, del_not16_8_q, del_not16_9_q, or_1_out;
  wire [6:0] controlled_buffer_1_out, controlled_buffer_2_out;
  wire [15:0] controlled_buffer_3_out;

  LED ELED (.in(E));
  DEL_NOT16 del_not16_1 (.Q(E), .D(del_not16_2_q));
  DEL_NOT16 del_not16_2 (.Q(del_not16_2_q), .D(del_not16_3_q));
  DEL_NOT16 del_not16_3 (.Q(del_not16_3_q), .D(decoder_1_out3));
  Register #(.width(7)) XREG (
    .D(controlled_buffer_1_out), .en(decoder_1_out1), .clk(del_not16_5_q), .Q(X));  // open: clr
  DEL_NOT16 del_not16_4 (.Q(del_not16_4_q), .D(decoder_1_out1));
  DEL_NOT16 del_not16_5 (.Q(del_not16_5_q), .D(del_not16_4_q));
  Register #(.width(7)) YREG (
    .D(controlled_buffer_2_out), .en(decoder_1_out2), .clk(del_not16_7_q), .Q(Y));  // open: clr
  DEL_NOT16 del_not16_6 (.Q(del_not16_6_q), .D(decoder_1_out2));
  DEL_NOT16 del_not16_7 (.Q(del_not16_7_q), .D(del_not16_6_q));
  Register #(.width(16)) DREG (
    .D(controlled_buffer_3_out), .en(decoder_1_out3), .clk(del_not16_9_q), .Q(D));  // open: clr
  DEL_NOT16 del_not16_8 (.Q(del_not16_8_q), .D(decoder_1_out3));
  DEL_NOT16 del_not16_9 (.Q(del_not16_9_q), .D(del_not16_8_q));
  assign controlled_buffer_1_out = decoder_1_out1 ? INSTR[8:2] : 7'bz;  // Controlled_Buffer controlled_buffer_1
  assign controlled_buffer_2_out = decoder_1_out2 ? INSTR[8:2] : 7'bz;  // Controlled_Buffer controlled_buffer_2
  assign controlled_buffer_3_out = decoder_1_out3 ? INSTR : 16'bz;  // Controlled_Buffer controlled_buffer_3
  or or_1 (or_1_out, INSTR[1], INSTR[0]);
  Decoder #(.select(2)) decoder_1 (
    .out0(R), .out1(decoder_1_out1), .out2(decoder_1_out2), .out3(decoder_1_out3), .sel(INSTR[1:0]),
    .en(or_1_out));
  // Probe on INSTR[8:2]
  // Probe on INSTR

  // Notes on the sheet:
  //   10: LDY
  //   11: DATA/PRINT
  //   0: RST
  //   01: LDX
endmodule

module HWSTACK (
  input  [15:0] HWSTK_I,
  input  POP,
  input  PUSH,
  input  [15:0] RAM_O,
  output [15:0] HWSTK_O,
  output [15:0] RAM_ADDR_I,
  output [15:0] RAM_DATA_I
);

  wire del_not16_1_q, del_not16_2_q, del_not16_3_q, del_not16_4_q, del_not16_5_q, del_not16_6_q,
       del_not16_7_q, or_1_out, or_2_out;
  wire [7:0] counter_1_q, SP_q, subtractor_1_out;
  wire [15:0] controlled_buffer_1_out;

  DEL_NOT16 del_not16_1 (.Q(del_not16_1_q), .D(del_not16_2_q));
  DEL_NOT16 del_not16_2 (.Q(del_not16_2_q), .D(POP));
  Counter counter_1 (
    .load(POP), .up(PUSH), .count(or_1_out), .clk(or_1_out), .D(subtractor_1_out), .Q(counter_1_q));  // open: clr, carry
  or or_1 (or_1_out, del_not16_1_q, PUSH);
  LED LED_PUSH (.in(PUSH));
  LED LED_POP (.in(POP));
  DEL_NOT16 del_not16_3 (.Q(del_not16_3_q), .D(POP));
  DEL_NOT16 del_not16_4 (.Q(del_not16_4_q), .D(del_not16_3_q));
  Subtractor subtractor_1 (.a(SP_q), .b(8'h1), .out(subtractor_1_out));  // open: bin, bout
  or or_2 (or_2_out, del_not16_4_q, PUSH);
  Register #(.width(16)) STKOUT (
    .D(controlled_buffer_1_out), .en(del_not16_6_q), .clk(del_not16_6_q), .Q(HWSTK_O));  // open: clr
  DEL_NOT16 del_not16_5 (.Q(del_not16_5_q), .D(del_not16_4_q));
  DEL_NOT16 del_not16_6 (.Q(del_not16_6_q), .D(del_not16_5_q));
  Register SP (.D(counter_1_q), .en(del_not16_7_q), .clk(del_not16_7_q), .Q(SP_q));  // open: clr
  DEL_NOT16 del_not16_7 (.Q(del_not16_7_q), .D(or_2_out));
  assign controlled_buffer_1_out = POP ? RAM_O : 16'bz;  // Controlled_Buffer controlled_buffer_1
  assign RAM_ADDR_I = {{8{1'b0}}, SP_q};  // Bit_Extender bit_extender_1
  assign RAM_DATA_I = PUSH ? HWSTK_I : 16'bz;  // Controlled_Buffer controlled_buffer_2
endmodule

module sketch (
  input  R,
  input  E,
  input  I
);

  wire clock_1_out, flix16_cpu_1_ram_clk, flix16_cpu_1_ram_we, flix16_cpu_1_wo, rgb_video_1_p1,
       rgb_video_1_p3;
  wire [6:0] rgb_video_1_p4, rgb_video_1_p5;
  wire [15:0] flix16_cpu_1_into, flix16_cpu_1_ipout, flix16_cpu_1_ram_addr, flix16_cpu_1_ram_in, ram_1_dout,
       register_1_q, rgb_video_1_p6;
  wire [23:0] rom_1_data;

  Clock clock_1 (.out(clock_1_out));
  ROM #(.addrWidth(16), .dataWidth(24)) rom_1 (.addr(flix16_cpu_1_ipout), .data(rom_1_data));
  FLIX16_CPU flix16_cpu_1 (
    .IPOUT(flix16_cpu_1_ipout), .RAM_ADDR(flix16_cpu_1_ram_addr), .RAM_IN(flix16_cpu_1_ram_in),
    .RAM_WE(flix16_cpu_1_ram_we), .RAM_CLK(flix16_cpu_1_ram_clk), .WO(flix16_cpu_1_wo),
    .INTO(flix16_cpu_1_into), .CTR_RST(R), .E(E), .INSTR(rom_1_data), .RAM_OUT(ram_1_dout),
    .CLK(clock_1_out), .INT1(I));  // open: EXTIN
  Pull_Resistor pull_resistor_1 (.node(flix16_cpu_1_into));
  Pull_Resistor pull_resistor_2 (.node(flix16_cpu_1_wo));
  // RGB_Video #(.reset("Synchronous"), .scale(3)) rgb_video_1: pin names not known; wires that end beside it: rgb_video_1_p1, clock_1_out, rgb_video_1_p3, rgb_video_1_p4, rgb_video_1_p5, rgb_video_1_p6
  DISPCTR dispctr_1 (
    .E(rgb_video_1_p3), .X(rgb_video_1_p4), .Y(rgb_video_1_p5), .D(rgb_video_1_p6), .R(rgb_video_1_p1),
    .INSTR(flix16_cpu_1_into));
  Register #(.width(16)) register_1 (
    .D(flix16_cpu_1_into), .en(flix16_cpu_1_wo), .clk(flix16_cpu_1_wo), .Q(register_1_q));  // open: clr
  Hex_Digit_Display hex_digit_display_1 (.value(register_1_q[15:12]));  // open: dp
  Hex_Digit_Display hex_digit_display_2 (.value(register_1_q[11:8]));  // open: dp
  Hex_Digit_Display hex_digit_display_3 (.value(register_1_q[7:4]));  // open: dp
  Hex_Digit_Display hex_digit_display_4 (.value(register_1_q[3:0]));  // open: dp
  RAM #(.addrWidth(16), .dataWidth(16), .enables("line")) ram_1 (
    .addr(flix16_cpu_1_ram_addr), .we(flix16_cpu_1_ram_we), .clk(flix16_cpu_1_ram_clk),
    .din(flix16_cpu_1_ram_in), .dout(ram_1_dout));

  // Notes on the sheet:
  //   contents of rom_1 (hex, n*v repeats v):
  //   100ff 30001 0 b0002 90000 170000 40000 30001 180002 0 150000
endmodule

module HWSTACK2 (
  input  [15:0] HWSTK_I,
  input  POP,
  input  PUSH,
  input  [15:0] RAM_O,
  output [15:0] HWSTK_O,
  output [15:0] RAM_ADDR_I,
  output RAM_WE,
  output RAM_CLK,
  output [15:0] RAM_DATA_I
);

  wire del_not16_1_q, del_not16_2_q, del_not16_3_q, del_not16_4_q, del_not16_5_q, del_not16_6_q,
       del_not16_7_q, del_not16_8_q, or_1_out, or_2_out;
  wire [7:0] counter_1_q, SP_q, subtractor_1_out;
  wire [15:0] controlled_buffer_1_out;

  DEL_NOT16 del_not16_1 (.Q(del_not16_1_q), .D(del_not16_2_q));
  DEL_NOT16 del_not16_2 (.Q(del_not16_2_q), .D(POP));
  Counter counter_1 (
    .load(POP), .up(PUSH), .count(or_1_out), .clk(or_1_out), .D(subtractor_1_out), .Q(counter_1_q));  // open: clr, carry
  or or_1 (or_1_out, del_not16_1_q, PUSH);
  LED LED_PUSH (.in(PUSH));
  LED LED_POP (.in(POP));
  DEL_NOT16 del_not16_3 (.Q(del_not16_3_q), .D(POP));
  DEL_NOT16 del_not16_4 (.Q(del_not16_4_q), .D(del_not16_3_q));
  Subtractor subtractor_1 (.a(SP_q), .b(8'h1), .out(subtractor_1_out));  // open: bin, bout
  or or_2 (or_2_out, del_not16_4_q, PUSH);
  Register #(.width(16)) STKOUT (
    .D(controlled_buffer_1_out), .en(del_not16_6_q), .clk(del_not16_6_q), .Q(HWSTK_O));  // open: clr
  DEL_NOT16 del_not16_5 (.Q(del_not16_5_q), .D(del_not16_4_q));
  DEL_NOT16 del_not16_6 (.Q(del_not16_6_q), .D(del_not16_5_q));
  Register SP (.D(counter_1_q), .en(del_not16_7_q), .clk(del_not16_7_q), .Q(SP_q));  // open: clr
  DEL_NOT16 del_not16_7 (.Q(del_not16_7_q), .D(or_2_out));
  assign controlled_buffer_1_out = POP ? RAM_O : 16'bz;  // Controlled_Buffer controlled_buffer_1
  assign RAM_ADDR_I = {{8{1'b0}}, SP_q};  // Bit_Extender bit_extender_1
  assign RAM_DATA_I = PUSH ? HWSTK_I : 16'bz;  // Controlled_Buffer controlled_buffer_2
  DEL_NOT16 del_not16_8 (.Q(del_not16_8_q), .D(PUSH));
  DEL_NOT16 del_not16_9 (.Q(RAM_CLK), .D(del_not16_8_q));

  assign RAM_WE = RAM_CLK;
endmodule
